# Fritzing sketch Schematic (saved by Fritzing 0.9.7b)
breadboards: 1

parts:
  R1 = Resistor [tolerance=±5% power=0.25 resistance=100 package=THT]
  U1 = Wio Terminal [package=2x40]
  LED1 = smd LED [color="Red (633nm)" current=0.030 package="0603 [SMD]"]

nets:
  N1: R1.Pin_0, U1.6
  N2: R1.Pin_1, LED1.cathode
  N3: U1.3, LED1.anode

notes:
  100Ω
