# Fritzing sketch button_external (saved by Fritzing 0.9.7b)
breadboards: 1

parts:
  U1 = Wio Terminal [package=2x40]
  IC1 = DIP - 8 pins [chip_label=IC package="DIP (Dual Inline) [THT]"]
  R1 = Resistor [tolerance=±5% power=0.25 resistance=220 package=THT]
  S1 = Momentary Switch [package=ksa_sealed_tac_switch]

nets:
  N1: U1.6, IC1.pin8, S1.4
  N2: U1.13, R1.Pin_0, S1.1
  N3: IC1.pin1, R1.Pin_1

custom parts:
  DIP - 8 pins: A DIP stand-in part for whatever IC you want. With 8 pins on a 300mil dual inline package (DIP) footprint.
