# Fritzing sketch Schematic (saved by Fritzing 0.9.7b)
breadboards: 1

parts:
  JP1 = M40 [package=1x40_offset]
  JP2 = M40 [package=1x40_offset]
  LED1 = LED - 5mm [color="Red (633nm)" current=0.030 package="5 mm [THT]"]
  R1 = Resistor [tolerance=±5% power=0.25 resistance=100 package=THT]

nets:
  N1: JP1.2, LED1.anode
  N2: JP2.3, R1.Pin_0
  N3: LED1.cathode, R1.Pin_1

notes:
  Wio Terminal ウラ面
  100Ω
  3番
  6番
