# Fritzing sketch stepper_motor_breadboard (saved by Fritzing 0.9.7b)
breadboards: 1

parts:
  U1 = Wio Terminal [package=2x40]
  M1 = Stepper Motor - Bipolar
  Pololu_A1 = Pololu A4988 [package=SO16]
  BATT1 = LiPoly Battery (1300mAh)
  Pololu_A2 = Pololu A4988 [package=SO16]
  M2 = Stepper Motor - Bipolar
  M3 = Stepper Motor - Bipolar
  Pololu_A3 = Pololu A4988 [package=SO16]
  パーツ1 = USB converter CP2102

nets:
  VDD: U1.2, Pololu_A1.VDD, Pololu_A2.VDD, Pololu_A3.VDD
  GND: U1.6, Pololu_A1.GND, BATT1.negative, Pololu_A2.GND, Pololu_A3.GND, パーツ1.GND
  N1: U1.8, パーツ1.RXI
  N2: U1.10, パーツ1.TXO
  N3: U1.13, Pololu_A1.DIR
  N4: U1.15, Pololu_A1.STEP
  N5: U1.16, Pololu_A3.DIR
  N6: U1.18, Pololu_A3.STEP
  N7: U1.22, Pololu_A2.DIR
  N8: U1.32, Pololu_A2.STEP
  N9: M1.A, Pololu_A1.2B
  N10: M1.C, Pololu_A1.2A
  N11: M1.B, Pololu_A1.1A
  N12: M1.D, Pololu_A1.1B
  N13: Pololu_A1.RESET, Pololu_A1.SLEEP
  N14: Pololu_A1.VMOT, BATT1.positive, Pololu_A2.VMOT, Pololu_A3.VMOT
  N15: Pololu_A2.RESET, Pololu_A2.SLEEP
  N16: Pololu_A2.1B, M2.D
  N17: Pololu_A2.1A, M2.B
  N18: Pololu_A2.2A, M2.C
  N19: Pololu_A2.2B, M2.A
  N20: M3.A, Pololu_A3.2B
  N21: M3.C, Pololu_A3.2A
  N22: M3.B, Pololu_A3.1A
  N23: M3.D, Pololu_A3.1B
  N24: Pololu_A3.RESET, Pololu_A3.SLEEP

notes:
  Wio Terminal
  バッテリーベース背面
  11.1V

custom parts:
  LiPoly Battery (1300mAh): Lithium Ion Polymer Battery (1300mAh)
