# Fritzing sketch stepper_motor_breadboard (saved by Fritzing 0.9.7b)
breadboards: 1

parts:
  U1 = Wio Terminal [package=2x40]
  M1 = Stepper Motor - Bipolar
  IC1 = DIP - 8 pins [chip_label=IC package="DIP (Dual Inline) [THT]"]
  Pololu_A1 = Pololu A4988 [package=SO16]

nets:
  N1: U1.2, Pololu_A1.VDD
  N2: U1.3, Pololu_A1.DIR
  N3: U1.5, Pololu_A1.STEP
  N4: U1.6, Pololu_A1.GND#8
  N5: M1.A, Pololu_A1.1B
  N6: M1.C, Pololu_A1.1A
  N7: M1.B, Pololu_A1.2A
  N8: M1.D, Pololu_A1.2B
  N9: IC1.pin1, Pololu_A1.VMOT
  N10: IC1.pin3, Pololu_A1.GND#14

notes:
  12V
  Wio Terminal
  バッテリーベース背面

custom parts:
  DIP - 8 pins: A DIP stand-in part for whatever IC you want. With 8 pins on a 300mil dual inline package (DIP) footprint.
