# Fritzing sketch stepper_motor_breadboard (saved by Fritzing 0.9.7b)
breadboards: 1

parts:
  IC3 = DIP - 8 pins [chip_label=IC package="DIP (Dual Inline) [THT]"]
  Board1 = L6470 Board [package="DIP16 [THT]"]
  U1 = Wio Terminal [package=2x40]
  M1 = Stepper Motor - Bipolar

nets:
  N1: IC3.pin5, Board1.cn1_vs
  N2: IC3.pin8, Board1.cn4_3, Board1.cn1_gnd, U1.6
  N3: Board1.cn4_1, U1.13
  N4: Board1.cn4_5, U1.21
  N5: Board1.cn4_6, U1.23
  N6: Board1.cn4_7, U1.19
  N7: Board1.cn4_8, U1.24
  N8: Board1.cn2_out1a, M1.A
  N9: Board1.cn2_out2a, M1.C
  N10: Board1.cn3_out1B, M1.B
  N11: Board1.cn3_out2B, M1.D

custom parts:
  DIP - 8 pins: A DIP stand-in part for whatever IC you want. With 8 pins on a 300mil dual inline package (DIP) footprint.
  L6470 Board: L6470 Drive Kit
