# Fritzing sketch breadboard (saved by Fritzing 0.9.7b)
breadboards: 1

parts:
  U2 = Wio Terminal [package=2x40]
  パーツ1 = USB converter CP2102
  U1 = CMA3000-A01 [package=cma3000]
  R1 = Resistor [tolerance=±5% power=0.25 resistance=10k package=THT]
  R2 = Resistor [tolerance=±5% power=0.25 resistance=10k package=THT]

nets:
  N1: U2.2, U1.VDD, R1.Pin_1, R2.Pin_1
  N2: U2.3, U1.VDD1, R1.Pin_0
  N3: U2.5, U1.Z, R2.Pin_0
  GND: U2.6, パーツ1.GND, U1.GND
  N4: U2.8, パーツ1.RXI
  N5: U2.10, パーツ1.TXO

notes:
  秋月電子通商
  BNO055 9軸センサ
  プルアップ抵抗
  10kΩ
