# Fritzing sketch breadboard (saved by Fritzing 0.9.7b)

parts:
  パーツ1 = Grove 8 Channel I2C Multiplexer
  パーツ2 = GY-VL53L0XV2 Laser Ranger Module
  パーツ3 = GY-VL53L0XV2 Laser Ranger Module
  U1 = Wio Terminal [package=2x40]
  パーツ4 = GY-VL53L0XV2 Laser Ranger Module
  パーツ5 = GY-VL53L0XV2 Laser Ranger Module
  パーツ6 = GY-VL53L0XV2 Laser Ranger Module
  パーツ7 = GY-VL53L0XV2 Laser Ranger Module
  パーツ8 = USB converter CP2102

nets:
  N1: パーツ1.i2c0_scl, パーツ3.SCL
  N2: パーツ1.i2c0_sda, パーツ3.SDA
  N3: パーツ1.i2c0_3v3, パーツ3.VCC
  N4: パーツ1.i2c0_gnd, パーツ3.GND
  N5: パーツ1.i2c1_scl, パーツ2.SCL
  N6: パーツ1.i2c1_sda, パーツ2.SDA
  N7: パーツ1.i2c1_3v3, パーツ2.VCC
  N8: パーツ1.i2c1_gnd, パーツ2.GND
  N9: パーツ1.i2c2_scl, パーツ4.SCL
  N10: パーツ1.i2c2_sda, パーツ4.SDA
  N11: パーツ1.i2c2_3v3, パーツ4.VCC
  N12: パーツ1.i2c2_gnd, パーツ4.GND
  N13: パーツ1.i2c3_scl, パーツ5.SCL
  N14: パーツ1.i2c3_sda, パーツ5.SDA
  N15: パーツ1.i2c3_3v3, パーツ5.VCC
  N16: パーツ1.i2c3_gnd, パーツ5.GND
  N17: パーツ1.i2c4_scl, パーツ6.SCL
  N18: パーツ1.i2c4_sda, パーツ6.SDA
  N19: パーツ1.i2c4_3v3, パーツ6.VCC
  N20: パーツ1.i2c4_gnd, パーツ6.GND
  N21: パーツ1.i2c5_scl, パーツ7.SCL
  N22: パーツ1.i2c5_sda, パーツ7.SDA
  N23: パーツ1.i2c5_3v3, パーツ7.VCC
  N24: パーツ1.i2c5_gnd, パーツ7.GND
  N25: U1.6, パーツ8.GND
  N26: U1.8, パーツ8.RXI
  N27: U1.10, パーツ8.TXO

custom parts:
  Grove 8 Channel I2C Multiplexer: I2C Mutiplexer
  GY-VL53L0XV2 Laser Ranger Module: The GY-VL53L0XV2 is based on the VL53L0X from ST Microelectronics, a time-of-flight ranging system integrated into a compact module.
