# Fritzing sketch breadboard (saved by Fritzing 0.9.7b)

parts:
  パーツ1 = Grove 8 Channel I2C Multiplexer
  パーツ2 = GY-VL53L0XV2 Laser Ranger Module
  パーツ3 = GY-VL53L0XV2 Laser Ranger Module
  U1 = Wio Terminal [package=2x40]  # not connected

nets:
  N1: パーツ1.i2c0_scl, パーツ3.SCL
  N2: パーツ1.i2c0_sda, パーツ3.SDA
  N3: パーツ1.i2c0_3v3, パーツ3.VCC
  N4: パーツ1.i2c0_gnd, パーツ3.GND
  N5: パーツ1.i2c1_scl, パーツ2.SCL
  N6: パーツ1.i2c1_sda, パーツ2.SDA
  N7: パーツ1.i2c1_3v3, パーツ2.VCC
  N8: パーツ1.i2c1_gnd, パーツ2.GND

custom parts:
  Grove 8 Channel I2C Multiplexer: I2C Mutiplexer
  GY-VL53L0XV2 Laser Ranger Module: The GY-VL53L0XV2 is based on the VL53L0X from ST Microelectronics, a time-of-flight ranging system integrated into a compact module.
