# Fritzing sketch breadboard (saved by Fritzing 0.9.7b)
breadboards: 1

parts:
  U1 = Wio Terminal [package=2x40]
  パーツ1 = USB converter CP2102
  パーツ2 = GY-VL53L0XV2 Laser Ranger Module

nets:
  N1: U1.2, パーツ2.VCC
  N2: U1.3, パーツ2.SDA
  N3: U1.5, パーツ2.SCL
  GND: U1.6, パーツ1.GND, パーツ2.GND
  N4: U1.8, パーツ1.RXI
  N5: U1.10, パーツ1.TXO
  N6: U1.33, パーツ2.GPIO1

notes:
  Wio Terminal
  バッテリーベース背面

custom parts:
  GY-VL53L0XV2 Laser Ranger Module: The GY-VL53L0XV2 is based on the VL53L0X from ST Microelectronics, a time-of-flight ranging system integrated into a compact module.
